# Fritzing sketch arduino_weather_sensors_v12 (saved by Fritzing 0.9.3b)
circuit board: 15.24cm x 15.24cm
breadboards: 1

parts:
  MPL3115A2 = MPL3115A2 I2C Barometric Pressure, Altitude, Temperature Sensor
  DHT11 = DHT11 Humitidy and Temperature Sensor
  Arduino_Uno = Arduino Uno (Rev3)
  Anemometer = IC, SIP package, 3 pins [chip_label=Wind]
  Raindrop_Sensor = IC, SIP package, 4 pins [chip_label=Rain]
  R1 = Resistor [tolerance=±5% resistance=220 package=THT]
  R4 = Resistor [tolerance=±5% resistance=220 package=THT]

nets:
  N1: MPL3115A2.VIN, R1.Pin_1
  GND: MPL3115A2.GND, DHT11.GND, Arduino_Uno.GND, Anemometer.pin2, Raindrop_Sensor.pin4
  N2: MPL3115A2.SCL, Arduino_Uno.A5/SCL
  N3: MPL3115A2.SDA, Arduino_Uno.A4/SDA
  VDD: DHT11.VDD, Arduino_Uno.5V, Anemometer.pin1, R1.Pin_0, R4.Pin_0
  N4: DHT11.DATA, Arduino_Uno.D2
  N5: Arduino_Uno.A0, Raindrop_Sensor.pin2
  N6: Arduino_Uno.A1, Anemometer.pin3
  N7: Raindrop_Sensor.pin3, R4.Pin_1

custom parts:
  MPL3115A2 I2C Barometric Pressure, Altitude, Temperature Sensor: This pressure sensor from Freescale is a great low-cost sensing solution for precision measurement of barometric pressure and altitude. The MPL3115A2 has a typical 1.5 Pascal resolution, which can resolve altitude at 0.3 meters (compare to the BMP180 which can do 0.17m). It has some upsides compared to the BMP180, such as interrupt outputs for ultra-low power usage, and its also a heck of a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
  DHT11 Humitidy and Temperature Sensor: DHT11 Humidity and Temperature Sensor
